# Fritzing sketch electrical (saved by Fritzing 0.9.3b)
breadboards: 1

parts:
  U1 = NodeMCU V1.0
  IC1 = L293D [package=THT]
  R1 = Resistor [tolerance=±5% resistance=120 package=THT]
  R2 = Resistor [tolerance=±5% resistance=360 package=THT]
  U2 = Voltage Regulator [package=to220-adj]
  U3 = LIPO-2000mAh [package=lipo-2000]
  R3 = Resistor [tolerance=±5% resistance=120 package=THT]
  R4 = Resistor [tolerance=±5% resistance=360 package=THT]
  U4 = Voltage Regulator [package=to220-adj]
  M1 = DC Motor
  M2 = DC Motor
  hc-sr1 = hc-sr04
  hc-sr2 = hc-sr04
  hc-sr3 = hc-sr04

nets:
  N1: U1.D0, IC1.In_1
  N2: U1.D1, U1.D5, U1.D6, U1.D7, U1.D8, U1.RX, U1.3V3, IC1.Enable_1, IC1.In_4, hc-sr1.Trig, hc-sr1.Echo, hc-sr2.Trig, hc-sr2.Echo
  N3: U1.D2, IC1.In_2
  N4: U1.D3, IC1.Enable_2
  N5: U1.D4, IC1.In_3
  N6: U1.SD2, hc-sr3.Trig
  N7: U1.SD3, hc-sr3.Echo
  N8: IC1.Out_1_(_Controlled_by_Enable_1_), M1.pin_1
  GND: IC1.0V, R1.Pin_0, U3.-, R3.Pin_0, hc-sr1.GND, hc-sr2.GND, hc-sr3.GND
  N9: IC1.Out_2_(_Controlled_by_Enable_1_), M1.pin_2
  N10: IC1.+Vmotor, U2.IN, U3.+, U4.IN
  N11: IC1.Out_3_(_Controlled_by_Enable_2_), M2.pin_2
  N12: IC1.Out_4_(_Controlled_by_Enable_2_), M2.pin_1
  N13: IC1.+V, R2.Pin_1, U2.OUT
  N14: R1.Pin_1, R2.Pin_0, U2.ADJ
  N15: R3.Pin_1, R4.Pin_0, U4.ADJ
  VCC: R4.Pin_1, U4.OUT, hc-sr1.VCC, hc-sr2.VCC, hc-sr3.VCC

custom parts:
  NodeMCU V1.0: ESP8266 based NodeMCU V1.0
